# Fritzing sketch schematic (saved by Fritzing 0.9.4)

parts:
  U1 = NodeMCU V3.0
  LED1 = LED - 5mm [color="Red (633nm)" package="5 mm [THT]"]
  R1 = Resistor [tolerance=±5% resistance=10k package=THT]
  S1 = Pushbutton [package=THT]
  R2 = Resistor [tolerance=±5% resistance=22 package=THT]

nets:
  N1: U1.D1, R2.Pin_1
  N2: U1.D2, R1.Pin_0, S1.leg1
  N3: U1.3V3, R1.Pin_1
  N4: U1.GND, LED1.cathode, S1.leg0
  N5: LED1.anode, R2.Pin_0

custom parts:
  NodeMCU V3.0: ESP8266 based NodeMCU
